// Logisim project 4BitAddierer.circ as structural Verilog: 3 circuits, main circuit main
module main (
  input  x4,
  input  y4,
  input  x3,
  input  y3,
  input  x2,
  input  y2,
  input  x1,
  input  y1,
  output s5,
  output s4,
  output s3,
  output s2,
  output s1
);

  wire HA_c, VA_2_c_out, VA_3_c_out;

  VA VA (.x(x4), .y(y4), .c_in(VA_2_c_out), .c_out(s5), .s(s4));
  VA VA_2 (.x(x3), .y(y3), .c_in(VA_3_c_out), .c_out(VA_2_c_out), .s(s3));
  VA VA_3 (.x(x2), .y(y2), .c_in(HA_c), .c_out(VA_3_c_out), .s(s2));
  HA HA (.x(x1), .y(y1), .c(HA_c), .s(s1));
endmodule

module HA (
  input  x,
  input  y,
  output c,
  output s
);

  wire and_2_out, and_3_out, not_1_out, not_2_out;

  and and_1 (c, x, y);
  not not_1 (not_1_out, x);
  and and_2 (and_2_out, not_1_out, y);
  and and_3 (and_3_out, x, not_2_out);
  not not_2 (not_2_out, y);
  or or_1 (s, and_2_out, and_3_out);
endmodule

module VA (
  input  x,
  input  y,
  input  c_in,
  output c_out,
  output s
);

  wire and_1_out, and_2_out, and_3_out, and_4_out, not_1_out, not_2_out, not_3_out;

  and and_1 (and_1_out, x, y, c_in);
  not not_1 (not_1_out, x);
  and and_2 (and_2_out, not_1_out, y, c_in);
  and and_3 (and_3_out, x, not_2_out, c_in);
  not not_2 (not_2_out, y);
  and and_4 (and_4_out, x, y, not_3_out);
  not not_3 (not_3_out, c_in);
  ExactlyOne xor_1 (.out(s), .in0(x), .in2(y), .in4(c_in));
  or or_1 (c_out, and_1_out, and_2_out, and_3_out, and_4_out);
endmodule
